// Logisim project DigitalClock.circ as structural Verilog: 2 circuits, main circuit main
module main (
);

  wire button_1_out, clock_1_out, invert5_out, invert6_out, invert8_out, inverter9_out, inverter10_out,
       iverter7_out, LSB1_qn, LSB2_qn, LSB3_qn, LSB4_qn, LSB5_qn, LSB_qn, MOD6_out, MOD6s2_out, MOD10_out,
       MOD10s2_out, MODE_q, nand_1_out, nand_2_out, nand_3_out, nand_4_out, nand_5_out, nand_6_out,
       nand_7_out, nand_8_out, Reset1_out, Reset_out, SetHourUnits_out, SetMinutesTens_out,
       SetMinutesUnits_out, SetSecondsTens_out, t_ff_1_qn, t_ff_2_qn, t_ff_3_qn, t_ff_5_qn, t_ff_6_qn,
       t_ff_7_qn, t_ff_8_qn, t_ff_9_qn, t_ff_11_qn, t_ff_12_qn, t_ff_13_qn, t_ff_14_qn, t_ff_15_qn,
       t_ff_16_qn;
  wire [2:0] LSB1_q, LSB3_q, LSB5_q, t_ff_1_q;
  wire [3:0] LSB2_q, LSB4_q, LSB_q, multiplexer_1_out, multiplexer_2_out, t_ff_5_q;

  T_Flip_Flop LSB5 (.T(1'b1), .clk(nand_2_out), .Q(LSB5_q[0]), .Qn(LSB5_qn), .reset(inverter9_out));  // open: preset
  T_Flip_Flop t_ff_1 (
    .T(1'b1), .clk(nand_4_out), .Q(t_ff_1_q[0]), .Qn(t_ff_1_qn), .reset(inverter10_out));  // open: preset
  T_Flip_Flop t_ff_2 (.T(1'b1), .clk(LSB5_qn), .Q(LSB5_q[1]), .Qn(t_ff_2_qn), .reset(inverter9_out));  // open: preset
  T_Flip_Flop t_ff_3 (
    .T(1'b1), .clk(t_ff_1_qn), .Q(t_ff_1_q[1]), .Qn(t_ff_3_qn), .reset(inverter10_out));  // open: preset
  Multiplexer #(.width(4)) multiplexer_1 (
    .in0({1'b0, t_ff_1_q}), .in1({1'b0, LSB5_q}), .out(multiplexer_1_out), .sel(MODE_q));
  T_Flip_Flop MSB5 (.T(1'b1), .clk(t_ff_2_qn), .Q(LSB5_q[2]), .reset(inverter9_out));  // open: Qn, preset
  nand inverter9 (inverter9_out, Reset_out, Reset_out);
  T_Flip_Flop t_ff_4 (.T(1'b1), .clk(t_ff_3_qn), .Q(t_ff_1_q[2]), .reset(inverter10_out));  // open: Qn, preset
  nand inverter10 (inverter10_out, nand_1_out, nand_1_out);
  Hex_Digit_Display hex_digit_display_1 (.value(multiplexer_1_out));  // open: dp
  T_Flip_Flop MODE (.T(1'b1), .clk(button_1_out), .Q(MODE_q));  // open: Qn, reset, preset
  Button button_1 (.out(button_1_out));
  nand Reset (Reset_out, LSB5_q[1], LSB4_q[2]);
  nand nand_1 (nand_1_out, t_ff_1_q[0], t_ff_5_q[1]);
  Hex_Digit_Display hex_digit_display_2 (.value(multiplexer_2_out));  // open: dp
  T_Flip_Flop LSB4 (.T(1'b1), .clk(MOD6s2_out), .Q(LSB4_q[0]), .Qn(LSB4_qn), .reset(Reset1_out));  // open: preset
  T_Flip_Flop t_ff_5 (.T(1'b1), .clk(MOD6s2_out), .Q(t_ff_5_q[0]), .Qn(t_ff_5_qn), .reset(nand_3_out));  // open: preset
  Multiplexer #(.width(4)) multiplexer_2 (.in0(t_ff_5_q), .in1(LSB4_q), .out(multiplexer_2_out), .sel(MODE_q));
  T_Flip_Flop t_ff_6 (.T(1'b1), .clk(LSB4_qn), .Q(LSB4_q[1]), .Qn(t_ff_6_qn), .reset(Reset1_out));  // open: preset
  T_Flip_Flop t_ff_7 (.T(1'b1), .clk(t_ff_5_qn), .Q(t_ff_5_q[1]), .Qn(t_ff_7_qn), .reset(nand_3_out));  // open: preset
  T_Flip_Flop t_ff_8 (.T(1'b1), .clk(t_ff_6_qn), .Q(LSB4_q[2]), .Qn(t_ff_8_qn), .reset(Reset1_out));  // open: preset
  T_Flip_Flop t_ff_9 (.T(1'b1), .clk(t_ff_7_qn), .Q(t_ff_5_q[2]), .Qn(t_ff_9_qn), .reset(nand_3_out));  // open: preset
  T_Flip_Flop MSB4 (.T(1'b1), .clk(t_ff_8_qn), .Q(LSB4_q[3]), .reset(Reset1_out));  // open: Qn, preset
  T_Flip_Flop t_ff_10 (.T(1'b1), .clk(t_ff_9_qn), .Q(t_ff_5_q[3]), .reset(nand_3_out));  // open: Qn, preset
  nand Reset1 (Reset1_out, nand_2_out, Reset_out);
  nand nand_2 (nand_2_out, LSB4_q[3], LSB4_q[1]);
  nand nand_3 (nand_3_out, nand_4_out, nand_1_out);
  nand nand_4 (nand_4_out, t_ff_5_q[3], t_ff_5_q[1]);
  T_Flip_Flop LSB3 (.T(1'b1), .clk(MOD10s2_out), .Q(LSB3_q[0]), .Qn(LSB3_qn), .reset(MOD6s2_out));  // open: preset
  T_Flip_Flop t_ff_11 (.T(1'b1), .clk(LSB3_qn), .Q(LSB3_q[1]), .Qn(t_ff_11_qn), .reset(MOD6s2_out));  // open: preset
  Hex_Digit_Display hex_digit_display_3 (.value({1'b0, LSB3_q}));  // open: dp
  T_Flip_Flop MSB3 (.T(1'b1), .clk(t_ff_11_qn), .Q(LSB3_q[2]), .reset(MOD6s2_out));  // open: Qn, preset
  nand nand_5 (nand_5_out, LSB3_q[2], LSB3_q[1]);
  nand MOD6s2 (MOD6s2_out, nand_5_out, invert8_out);
  nand invert8 (invert8_out, SetHourUnits_out, SetHourUnits_out);
  Button SetHourUnits (.out(SetHourUnits_out));
  T_Flip_Flop LSB2 (.T(1'b1), .clk(MOD6_out), .Q(LSB2_q[0]), .Qn(LSB2_qn), .reset(MOD10s2_out));  // open: preset
  T_Flip_Flop t_ff_12 (.T(1'b1), .clk(LSB2_qn), .Q(LSB2_q[1]), .Qn(t_ff_12_qn), .reset(MOD10s2_out));  // open: preset
  Hex_Digit_Display hex_digit_display_4 (.value(LSB2_q));  // open: dp
  T_Flip_Flop t_ff_13 (
    .T(1'b1), .clk(t_ff_12_qn), .Q(LSB2_q[2]), .Qn(t_ff_13_qn), .reset(MOD10s2_out));  // open: preset
  T_Flip_Flop MSB2 (.T(1'b1), .clk(t_ff_13_qn), .Q(LSB2_q[3]), .reset(MOD10s2_out));  // open: Qn, preset
  nand MOD10s2 (MOD10s2_out, nand_6_out, invert6_out);
  nand nand_6 (nand_6_out, LSB2_q[3], LSB2_q[1]);
  nand invert6 (invert6_out, SetMinutesTens_out, SetMinutesTens_out);
  Button SetMinutesTens (.out(SetMinutesTens_out));
  T_Flip_Flop LSB1 (.T(1'b1), .clk(MOD10_out), .Q(LSB1_q[0]), .Qn(LSB1_qn), .reset(MOD6_out));  // open: preset
  T_Flip_Flop t_ff_14 (.T(1'b1), .clk(LSB1_qn), .Q(LSB1_q[1]), .Qn(t_ff_14_qn), .reset(MOD6_out));  // open: preset
  Hex_Digit_Display hex_digit_display_5 (.value({1'b0, LSB1_q}));  // open: dp
  T_Flip_Flop MSB1 (.T(1'b1), .clk(t_ff_14_qn), .Q(LSB1_q[2]), .reset(MOD6_out));  // open: Qn, preset
  nand MOD6 (MOD6_out, nand_7_out, iverter7_out);
  nand nand_7 (nand_7_out, LSB1_q[2], LSB1_q[1]);
  nand iverter7 (iverter7_out, SetMinutesUnits_out, SetMinutesUnits_out);
  Button SetMinutesUnits (.out(SetMinutesUnits_out));
  T_Flip_Flop LSB (.T(1'b1), .clk(clock_1_out), .Q(LSB_q[0]), .Qn(LSB_qn), .reset(MOD10_out));  // open: preset
  Clock clock_1 (.out(clock_1_out));
  Hex_Digit_Display hex_digit_display_6 (.value(LSB_q));  // open: dp
  T_Flip_Flop t_ff_15 (.T(1'b1), .clk(LSB_qn), .Q(LSB_q[1]), .Qn(t_ff_15_qn), .reset(MOD10_out));  // open: preset
  T_Flip_Flop t_ff_16 (.T(1'b1), .clk(t_ff_15_qn), .Q(LSB_q[2]), .Qn(t_ff_16_qn), .reset(MOD10_out));  // open: preset
  T_Flip_Flop MSB (.T(1'b1), .clk(t_ff_16_qn), .Q(LSB_q[3]), .reset(MOD10_out));  // open: Qn, preset
  nand nand_8 (nand_8_out, LSB_q[3], LSB_q[1]);
  nand MOD10 (MOD10_out, nand_8_out, invert5_out);
  nand invert5 (invert5_out, SetSecondsTens_out, SetSecondsTens_out);
  Button SetSecondsTens (.out(SetSecondsTens_out));
endmodule

module BCD2 (
  input  I3,
  input  I2,
  input  I1,
  input  I0,
  output a,
  output b,
  output c,
  output d,
  output e,
  output f,
  output g
);

  wire nand_1_out, nand_2_out, nand_3_out, nand_4_out, nand_5_out, nand_6_out, nand_7_out, nand_8_out,
       nand_9_out, nand_11_out, nand_12_out, nand_13_out, nand_14_out, nand_15_out, nand_16_out, nand_17_out,
       nand_18_out, nand_19_out, nand_20_out, nand_21_out, nand_22_out;

  nand nand_1 (nand_1_out, 1'b1, I3);
  nand nand_2 (nand_2_out, 1'b1, I2);
  nand nand_3 (nand_3_out, 1'b1, I1);
  nand nand_4 (nand_4_out, 1'b1, I0);
  nand nand_5 (nand_5_out, nand_2_out, nand_4_out);
  nand nand_6 (nand_6_out, I2, I0);
  nand nand_7 (nand_7_out, nand_2_out, I1);
  nand nand_8 (nand_8_out, nand_3_out, nand_4_out);
  nand nand_9 (nand_9_out, I1, I0);
  nand nand_10 (c, I1, nand_4_out, nand_2_out);
  nand nand_11 (nand_11_out, nand_2_out, nand_4_out);
  nand nand_12 (nand_12_out, nand_2_out, I1);
  nand nand_13 (nand_13_out, I2, nand_3_out, I0);
  nand nand_14 (nand_14_out, I1, nand_4_out);
  nand nand_15 (nand_15_out, nand_2_out, nand_4_out);
  nand nand_16 (nand_16_out, I1, nand_4_out);
  nand nand_17 (nand_17_out, nand_3_out, nand_4_out);
  nand nand_18 (nand_18_out, I2, nand_3_out);
  nand nand_19 (nand_19_out, I2, nand_4_out);
  nand nand_20 (nand_20_out, nand_2_out, I1);
  nand nand_21 (nand_21_out, I2, nand_3_out);
  nand nand_22 (nand_22_out, I1, nand_4_out);
  nand nand_23 (a, nand_5_out, nand_6_out, nand_1_out, nand_7_out);
  nand nand_24 (b, I2, nand_8_out, nand_9_out);
  nand nand_25 (d, nand_11_out, nand_12_out, nand_13_out, nand_14_out);
  nand nand_26 (e, nand_15_out, nand_16_out);
  nand nand_27 (f, nand_17_out, nand_18_out, nand_19_out, nand_1_out);
  nand nand_28 (g, nand_20_out, nand_21_out, nand_1_out, nand_22_out);
endmodule
